// Logisim project Circuit.circ as structural Verilog
module half_adder (
  input  A,
  input  B,
  output sum,
  output carry_out
);

  xor xor_1 (sum, A, B);
  and and_1 (carry_out, A, B);
endmodule

module full_adder (
  input  A,
  input  B,
  input  Cin,
  output Sum_out,
  output carry_out
);

  wire half_adder_1_carry_out, half_adder_1_sum, half_adder_2_carry_out;

  half_adder half_adder_1 (.A(A), .B(B), .sum(half_adder_1_sum), .carry_out(half_adder_1_carry_out));
  half_adder half_adder_2 (.A(half_adder_1_sum), .B(Cin), .sum(Sum_out), .carry_out(half_adder_2_carry_out));
  or or_1 (carry_out, half_adder_2_carry_out, half_adder_1_carry_out);
endmodule

module two_bit_adder (
  input  cin,
  input  [1:0] A,
  input  [1:0] B,
  output [1:0] sum_out,
  output carry_out
);

  wire full_adder_1_carry_out;

  full_adder full_adder_1 (.A(A[0]), .B(B[0]), .Cin(cin), .Sum_out(sum_out[0]), .carry_out(full_adder_1_carry_out));
  full_adder full_adder_2 (
    .A(A[1]), .B(B[1]), .Cin(full_adder_1_carry_out), .Sum_out(sum_out[1]), .carry_out(carry_out));
endmodule

module four_bit_adder (
  input  cin,
  input  [3:0] A,
  input  [3:0] B,
  output [3:0] sum_out,
  output cout
);

  wire two_bit_adder_1_carry_out;

  two_bit_adder two_bit_adder_1 (
    .cin(cin), .A(A[1:0]), .B(B[1:0]), .sum_out(sum_out[1:0]), .carry_out(two_bit_adder_1_carry_out));
  two_bit_adder two_bit_adder_2 (
    .cin(two_bit_adder_1_carry_out), .A(A[3:2]), .B(B[3:2]), .sum_out(sum_out[3:2]), .carry_out(cout));
endmodule

module eight_bit_adder (
  input  cin,
  input  [7:0] A,
  input  [7:0] B,
  output [7:0] sum_out,
  output cout
);

  wire four_bit_adder_1_cout;

  four_bit_adder four_bit_adder_1 (
    .cin(cin), .A(A[3:0]), .B(B[3:0]), .sum_out(sum_out[3:0]), .cout(four_bit_adder_1_cout));
  four_bit_adder four_bit_adder_2 (
    .cin(four_bit_adder_1_cout), .A(A[7:4]), .B(B[7:4]), .sum_out(sum_out[7:4]), .cout(cout));
endmodule

module sixteen_bit_adder (
  input  cin,
  input  [15:0] A,
  input  [15:0] B,
  output [15:0] sum_out,
  output cout
);

  wire eight_bit_adder_1_cout;

  eight_bit_adder eight_bit_adder_1 (
    .cin(cin), .A(A[7:0]), .B(B[7:0]), .sum_out(sum_out[7:0]), .cout(eight_bit_adder_1_cout));
  eight_bit_adder eight_bit_adder_2 (
    .cin(eight_bit_adder_1_cout), .A(A[15:8]), .B(B[15:8]), .sum_out(sum_out[15:8]), .cout(cout));
endmodule

module thirtyTwo_bit_Adder (
  input  cin,
  input  [31:0] A,
  input  [31:0] B,
  output [31:0] sum_out,
  output cout
);

  wire sixteen_bit_adder_1_cout;

  sixteen_bit_adder sixteen_bit_adder_1 (
    .cin(cin), .A(A[15:0]), .B(B[15:0]), .sum_out(sum_out[15:0]), .cout(sixteen_bit_adder_1_cout));
  sixteen_bit_adder sixteen_bit_adder_2 (
    .cin(sixteen_bit_adder_1_cout), .A(A[31:16]), .B(B[31:16]), .sum_out(sum_out[31:16]), .cout(cout));
endmodule

module sixtyFour_bit_Adder (
  input  cin,
  input  [63:0] A,
  input  [63:0] B,
  output [63:0] sum_out,
  output cout
);

  wire thirtytwo_bit_adder_1_cout;

  thirtyTwo_bit_Adder thirtytwo_bit_adder_1 (
    .cin(cin), .A(A[31:0]), .B(B[31:0]), .sum_out(sum_out[31:0]), .cout(thirtytwo_bit_adder_1_cout));
  thirtyTwo_bit_Adder thirtytwo_bit_adder_2 (
    .cin(thirtytwo_bit_adder_1_cout), .A(A[63:32]), .B(B[63:32]), .sum_out(sum_out[63:32]), .cout(cout));
endmodule

module matrixAdder2x2Core (
  input  [63:0] A11,
  input  [63:0] A12,
  input  [63:0] A21,
  input  [63:0] A22,
  input  [63:0] B11,
  input  [63:0] B12,
  input  [63:0] B21,
  input  [63:0] B22,
  output [63:0] R11,
  output [63:0] R12,
  output [63:0] R22,
  output [63:0] R21
);

  sixtyFour_bit_Adder Node_1 (.A(A11), .B(B11), .sum_out(R11));  // open: cin, cout
  sixtyFour_bit_Adder Node_3 (.A(A21), .B(B21), .sum_out(R21));  // open: cin, cout
  sixtyFour_bit_Adder Node_2 (.A(A12), .B(B12), .sum_out(R12));  // open: cin, cout
  sixtyFour_bit_Adder Node_4 (.A(A22), .B(B22), .sum_out(R22));  // open: cin, cout
endmodule

module testBench (
  input  [63:0] in_1,
  input  [63:0] in_2,
  input  [63:0] in_3,
  input  [63:0] in_4,
  input  [63:0] in_5,
  input  [63:0] in_6,
  input  [63:0] in_7,
  input  [63:0] in_8,
  output [63:0] out_9,
  output [63:0] out_10,
  output [63:0] out_11,
  output [63:0] out_12
);

  matrixAdder2x2Core matrixadder2x2core_1 (
    .A11(in_1), .A12(in_2), .A21(in_3), .A22(in_4), .B11(in_5), .B12(in_7), .B21(in_8), .B22(in_6),
    .R11(out_9), .R12(out_10), .R22(out_11), .R21(out_12));
endmodule

module Assembly (
  input  OUTPUT_ENABLE,
  input  WRITE_ENABLE
);

  wire clock_1_out, Delay_Counter_carry;
  wire [3:0] counter_1_q;
  wire [63:0] matrixadder2x2core_1_r11, matrixadder2x2core_1_r12, matrixadder2x2core_1_r21,
       matrixadder2x2core_1_r22, RAM_A11_dout, RAM_A12_dout, RAM_A21_dout, RAM_A22_dout, RAM_B11_dout,
       RAM_B12_dout, RAM_B21_dout, RAM_B22_dout;

  Clock clock_1 (.out(clock_1_out));
  RAM #(.addrWidth(4), .dataWidth(64), .\type ("nonvolatile")) RAM_A11 (
    .addr(counter_1_q), .oe(1'b1), .clk(clock_1_out), .dout(RAM_A11_dout));  // open: we, din
  Counter #(.max('h2), .width(4)) Delay_Counter (
    .count(clock_1_out), .clk(clock_1_out), .carry(Delay_Counter_carry));  // open: clr, load, up, D, Q
  // Probe on RAM_A11_dout
  RAM #(.addrWidth(4), .dataWidth(64), .\type ("nonvolatile")) RAM_A12 (
    .addr(counter_1_q), .clk(clock_1_out), .dout(RAM_A12_dout));  // open: we, oe, din
  Counter #(.max('h3), .width(4)) counter_1 (
    .count(Delay_Counter_carry), .clk(clock_1_out), .Q(counter_1_q));  // open: clr, load, up, D, carry
  matrixAdder2x2Core matrixadder2x2core_1 (
    .A11(RAM_A11_dout), .A12(RAM_A12_dout), .A21(RAM_A21_dout), .A22(RAM_A22_dout), .B11(RAM_B11_dout),
    .B12(RAM_B12_dout), .B21(RAM_B21_dout), .B22(RAM_B22_dout), .R11(matrixadder2x2core_1_r11),
    .R12(matrixadder2x2core_1_r12), .R22(matrixadder2x2core_1_r22), .R21(matrixadder2x2core_1_r21));
  RAM #(.addrWidth(4), .dataWidth(64), .\type ("nonvolatile")) RAM_A21 (
    .addr(counter_1_q), .oe(1'b1), .clk(clock_1_out), .dout(RAM_A21_dout));  // open: we, din
  // Probe on matrixadder2x2core_1_r11
  RAM #(.addrWidth(4), .dataWidth(64), .\type ("nonvolatile")) RAM_A22 (
    .addr(counter_1_q), .oe(1'b1), .clk(clock_1_out), .dout(RAM_A22_dout));  // open: we, din
  RAM #(.addrWidth(4), .dataWidth(64)) R_11 (
    .addr(counter_1_q), .we(1'b1), .clk(clock_1_out), .din(matrixadder2x2core_1_r11));  // open: oe, dout
  RAM #(.addrWidth(4), .dataWidth(64), .\type ("nonvolatile")) RAM_B11 (
    .addr(counter_1_q), .oe(1'b1), .clk(clock_1_out), .dout(RAM_B11_dout));  // open: we, din
  RAM #(.addrWidth(4), .dataWidth(64), .\type ("nonvolatile")) RAM_B12 (
    .addr(counter_1_q), .oe(1'b1), .clk(clock_1_out), .dout(RAM_B12_dout));  // open: we, din
  RAM #(.addrWidth(4), .dataWidth(64)) R_12 (
    .addr(counter_1_q), .we(1'b1), .clk(clock_1_out), .din(matrixadder2x2core_1_r12));  // open: oe, dout
  RAM #(.addrWidth(4), .dataWidth(64), .\type ("nonvolatile")) RAM_B21 (
    .addr(counter_1_q), .oe(1'b1), .clk(clock_1_out), .dout(RAM_B21_dout));  // open: we, din
  RAM #(.addrWidth(4), .dataWidth(64)) R_21 (
    .addr(counter_1_q), .we(1'b1), .clk(clock_1_out), .din(matrixadder2x2core_1_r21));  // open: oe, dout
  RAM #(.addrWidth(4), .dataWidth(64), .\type ("nonvolatile")) RAM_B22 (
    .addr(counter_1_q), .oe(1'b1), .clk(clock_1_out), .dout(RAM_B22_dout));  // open: we, din
  RAM #(.addrWidth(4), .dataWidth(64)) R_22 (
    .addr(counter_1_q), .we(1'b1), .clk(clock_1_out), .din(matrixadder2x2core_1_r22));  // open: oe, dout

  // Notes on the sheet:
  //   Matrix_A
  //   Matrix_B
endmodule

module counterdemo (
  input  in_1,
  input  in_2,
  input  in_3,
  input  in_4,
  input  [3:0] in_5,
  output [3:0] out_6
);

  Counter #(.max('h3), .ongoal("load"), .width(4)) counter_1 (
    .load(in_1), .up(in_2), .count(in_3), .clk(in_4), .D(in_5), .Q(out_6));  // open: clr, carry
endmodule
